// Logisim project Multi_bit_parity_checker.circ as structural Verilog: 1 circuit, main circuit main
module main (
  input  A3,
  input  A2,
  input  A1,
  input  A0,
  input  Pa,
  input  B3,
  input  B2,
  input  B1,
  input  B0,
  input  Pa_2,
  input  C3,
  input  C2,
  input  C1,
  input  C0,
  input  Pa_3,
  output StatusA,
  output StatusB,
  output StatusC,
  output Fault
);

  wire n7432_1__3__1y, n7486_1__3__1y, n7486_1__6__2y, n7486_1__8__3y, n7486_1__11__4y, n7486_2__3__1y,
       n7486_2__6__2y, n7486_2__8__3y, n7486_2__11__4y, n7486_3__3__1y, n7486_3__6__2y, n7486_3__8__3y,
       n7486_3__11__4y;

  _7486 u_7486_1 (
    ._1__1A(A2), ._2__1B(A3), ._3__1Y(n7486_1__3__1y), ._4__2A(n7486_1__3__1y), ._5__2B(A1),
    ._6__2Y(n7486_1__6__2y), ._7__GND(1'b0), ._14__Vcc(1'b1), ._13__4B(n7486_1__8__3y), ._12__4A(Pa),
    ._11__4Y(n7486_1__11__4y), ._10__3B(n7486_1__6__2y), ._9__3A(A0), ._8__3Y(n7486_1__8__3y));
  _7486 u_7486_2 (
    ._1__1A(B2), ._2__1B(B3), ._3__1Y(n7486_2__3__1y), ._4__2A(n7486_2__3__1y), ._5__2B(B1),
    ._6__2Y(n7486_2__6__2y), ._7__GND(1'b0), ._14__Vcc(1'b1), ._13__4B(n7486_2__8__3y), ._12__4A(Pa_2),
    ._11__4Y(n7486_2__11__4y), ._10__3B(n7486_2__6__2y), ._9__3A(B0), ._8__3Y(n7486_2__8__3y));
  _7404 u_7404_1 (
    ._1__1A(n7486_1__11__4y), ._2__1Y(StatusA), ._7__GND(1'b0), ._14__Vcc(1'b1), ._13__6A(n7486_2__11__4y),
    ._12__6Y(StatusB), ._11__5A(n7486_3__11__4y), ._10__5Y(StatusC));  // open: _3__2A, _4__2Y, _5__3A, _6__3Y, _9__4A, _8__4Y
  _7432 u_7432_1 (
    ._1__1A(n7486_2__11__4y), ._2__1B(n7486_1__11__4y), ._3__1Y(n7432_1__3__1y), ._4__2A(n7432_1__3__1y),
    ._5__2B(n7486_3__11__4y), ._6__2Y(Fault), ._7__GND(1'b0), ._14__Vcc(1'b1));  // open: _13__4B, _12__4A, _11__4Y, _10__3B, _9__3A, _8__3Y
  _7486 u_7486_3 (
    ._1__1A(C2), ._2__1B(C3), ._3__1Y(n7486_3__3__1y), ._4__2A(n7486_3__3__1y), ._5__2B(C1),
    ._6__2Y(n7486_3__6__2y), ._7__GND(1'b0), ._14__Vcc(1'b1), ._13__4B(n7486_3__8__3y), ._12__4A(Pa_3),
    ._11__4Y(n7486_3__11__4y), ._10__3B(n7486_3__6__2y), ._9__3A(C0), ._8__3Y(n7486_3__8__3y));
endmodule
